// Logisim project Sumator 5bitowy.circ as structural Verilog: 1 circuit, main circuit main
module main (
  input  in_1,
  input  in_2,
  input  in_3,
  input  in_4,
  input  in_5,
  input  in_6,
  input  in_7,
  input  in_8,
  input  in_9,
  input  in_10
);

  wire and_1_out, and_2_out, and_3_out, and_4_out, and_5_out, and_6_out, and_7_out, and_8_out, and_9_out,
       or_1_out, or_2_out, or_3_out, or_4_out, xor_1_out, xor_2_out, xor_3_out, xor_4_out, xor_5_out,
       xor_6_out, xor_7_out, xor_8_out, xor_9_out;

  LED led_1 (.in(xor_1_out));
  xor xor_1 (xor_1_out, in_1, in_6);
  LED led_2 (.in(and_1_out));
  and and_1 (and_1_out, in_1, in_6);
  xor xor_2 (xor_2_out, in_2, in_7);
  xor xor_3 (xor_3_out, xor_2_out, and_1_out);
  and and_2 (and_2_out, xor_2_out, and_1_out);
  and and_3 (and_3_out, in_2, in_7);
  LED led_3 (.in(xor_3_out));
  LED led_4 (.in(xor_1_out));
  LED led_5 (.in(xor_3_out));
  LED led_6 (.in(or_1_out));
  or or_1 (or_1_out, and_2_out, and_3_out);
  LED led_7 (.in(xor_5_out));
  LED led_8 (.in(xor_9_out));
  LED led_9 (.in(xor_7_out));
  xor xor_4 (xor_4_out, in_3, in_8);
  LED led_10 (.in(or_4_out));
  xor xor_5 (xor_5_out, xor_4_out, or_1_out);
  and and_4 (and_4_out, xor_4_out, or_1_out);
  and and_5 (and_5_out, in_3, in_8);
  or or_2 (or_2_out, and_4_out, and_5_out);
  LED led_11 (.in(xor_5_out));
  LED led_12 (.in(or_2_out));
  xor xor_6 (xor_6_out, in_4, in_9);
  xor xor_7 (xor_7_out, xor_6_out, or_2_out);
  and and_6 (and_6_out, xor_6_out, or_2_out);
  and and_7 (and_7_out, in_4, in_9);
  LED led_13 (.in(xor_7_out));
  LED led_14 (.in(or_3_out));
  or or_3 (or_3_out, and_6_out, and_7_out);
  xor xor_8 (xor_8_out, in_5, in_10);
  xor xor_9 (xor_9_out, xor_8_out, or_3_out);
  and and_8 (and_8_out, xor_8_out, or_3_out);
  and and_9 (and_9_out, in_5, in_10);
  LED led_15 (.in(xor_9_out));
  or or_4 (or_4_out, and_8_out, and_9_out);
  LED led_16 (.in(or_4_out));

  // Notes on the sheet:
  //   wynik 1 bit
  //   wynik 2bit
  //   wynik 3bit
  //   wynik 4bit
  //   wynik 5bit
  //   wynik 6bit
endmodule
