// Logisim project SumatorProjekt.circ as structural Verilog: 1 circuit, main circuit main
module main (
  input  in_1,
  input  in_2,
  input  in_3,
  input  in_4,
  input  in_5,
  input  in_6,
  input  in_7,
  input  in_8,
  output a,
  output b,
  output c,
  output d,
  output e,
  output f,
  output g,
  output a_2,
  output b_2,
  output c_2,
  output d_2,
  output e_2,
  output f_2,
  output g_2
);

  wire and_1_out, and_2_out, and_3_out, and_4_out, and_5_out, and_6_out, and_7_out, and_8_out, and_9_out,
       and_10_out, and_11_out, and_12_out, and_13_out, and_14_out, and_15_out, and_16_out, and_17_out,
       and_18_out, and_19_out, and_20_out, and_21_out, and_22_out, and_23_out, and_24_out, and_25_out,
       and_26_out, and_27_out, and_28_out, and_29_out, and_30_out, and_31_out, and_32_out, and_33_out,
       and_34_out, and_35_out, and_36_out, and_37_out, and_38_out, and_39_out, and_40_out, and_42_out,
       and_43_out, not_1_out, not_2_out, not_3_out, not_4_out, not_5_out, not_6_out, not_7_out, not_8_out,
       not_9_out, not_10_out, not_11_out, not_12_out, not_13_out, not_14_out, not_15_out, not_16_out,
       not_17_out, not_18_out, not_19_out, not_20_out, not_21_out, not_22_out, not_23_out, not_24_out,
       not_25_out, not_26_out, not_27_out, not_28_out, not_29_out, not_30_out, not_31_out, not_32_out,
       not_33_out, not_34_out, not_35_out, not_36_out, not_37_out, not_38_out, not_39_out, not_40_out,
       not_41_out, not_42_out, not_43_out, not_44_out, not_45_out, not_46_out, not_47_out, not_48_out,
       not_50_out, not_51_out, not_52_out, or_2_out, or_3_out, or_4_out, or_5_out, or_6_out, or_7_out,
       or_18_out, xor_1_out, xor_2_out, xor_3_out, xor_4_out, xor_5_out, xor_6_out, xor_7_out;

  xor xor_1 (xor_1_out, in_4, in_8);
  LED led_1 (.in(xor_1_out));
  and and_1 (and_1_out, in_4, in_8);
  xor xor_2 (xor_2_out, in_3, in_7);
  and and_2 (and_2_out, or_18_out, xor_5_out);
  and and_3 (and_3_out, or_18_out, xor_7_out);
  not not_1 (not_1_out, or_18_out);
  not not_2 (not_2_out, or_18_out);
  not not_3 (not_3_out, xor_7_out);
  not not_4 (not_4_out, xor_5_out);
  not not_5 (not_5_out, or_18_out);
  not not_6 (not_6_out, xor_5_out);
  not not_7 (not_7_out, xor_3_out);
  not not_8 (not_8_out, xor_7_out);
  not not_9 (not_9_out, xor_5_out);
  not not_10 (not_10_out, xor_3_out);
  not not_11 (not_11_out, or_18_out);
  not not_12 (not_12_out, xor_7_out);
  not not_13 (not_13_out, or_18_out);
  not not_14 (not_14_out, xor_5_out);
  not not_15 (not_15_out, xor_3_out);
  not not_16 (not_16_out, xor_5_out);
  not not_17 (not_17_out, or_18_out);
  not not_18 (not_18_out, xor_7_out);
  not not_19 (not_19_out, xor_7_out);
  not not_20 (not_20_out, or_18_out);
  not not_21 (not_21_out, xor_3_out);
  not not_22 (not_22_out, xor_7_out);
  not not_23 (not_23_out, xor_5_out);
  not not_24 (not_24_out, xor_3_out);
  not not_25 (not_25_out, xor_5_out);
  _7_Segment_Display u_7_segment_display_1 (
    .g(g_2), .f(f_2), .a(a_2), .b(1'b1), .e(e_2), .d(d_2), .c(c_2));  // open: dp
  xor xor_3 (xor_3_out, xor_2_out, and_1_out);
  and and_4 (and_4_out, xor_2_out, and_1_out);
  and and_5 (and_5_out, in_3, in_7);
  or or_1 (g_2, and_2_out, and_3_out);
  and and_6 (and_6_out, not_1_out, xor_7_out, xor_3_out);
  and and_7 (and_7_out, not_2_out, xor_7_out, xor_5_out);
  and and_8 (and_8_out, xor_7_out, xor_5_out, xor_3_out);
  and and_9 (and_9_out, or_18_out, not_3_out, not_4_out);
  and and_10 (and_10_out, not_5_out, xor_7_out, not_6_out, not_7_out);
  and and_11 (and_11_out, or_18_out, not_8_out, not_9_out, xor_3_out);
  and and_12 (and_12_out, or_18_out, xor_7_out, xor_5_out, not_10_out);
  and and_13 (and_13_out, not_11_out, not_12_out, xor_5_out);
  and and_14 (and_14_out, not_13_out, xor_5_out, xor_3_out);
  and and_15 (and_15_out, or_18_out, not_14_out, not_15_out);
  and and_16 (and_16_out, or_18_out, xor_7_out, not_16_out);
  and and_17 (and_17_out, not_17_out, not_18_out, xor_3_out);
  and and_18 (and_18_out, not_19_out, xor_5_out, xor_3_out);
  and and_19 (and_19_out, not_20_out, xor_7_out, xor_5_out, not_21_out);
  and and_20 (and_20_out, or_18_out, not_22_out, not_23_out, not_24_out);
  and and_21 (and_21_out, or_18_out, xor_7_out, not_25_out, xor_3_out);
  LED led_2 (.in(xor_3_out));
  or or_2 (or_2_out, and_4_out, and_5_out);
  LED led_3 (.in(g_2));
  LED led_4 (.in(or_3_out));
  or or_3 (or_3_out, and_6_out, and_7_out, and_8_out, and_9_out);
  or or_4 (or_4_out, and_10_out, and_11_out, and_12_out);
  LED led_5 (.in(or_4_out));
  LED led_6 (.in(or_5_out));
  or or_5 (or_5_out, and_13_out, and_14_out, and_15_out, and_16_out);
  or or_6 (or_6_out, and_17_out, and_18_out, and_19_out, and_20_out, and_21_out);
  LED led_7 (.in(or_6_out));
  LED led_8 (.in(xor_1_out));
  _7_Segment_Display u_7_segment_display_2 (.g(g), .f(f), .a(a), .b(b), .e(e), .d(d), .c(c));  // open: dp
  xor xor_4 (xor_4_out, in_2, in_6);
  xor xor_5 (xor_5_out, xor_4_out, or_2_out);
  and and_22 (and_22_out, xor_4_out, or_2_out);
  and and_23 (and_23_out, in_2, in_6);
  LED led_9 (.in(xor_5_out));
  or or_7 (or_7_out, and_22_out, and_23_out);
  not not_26 (not_26_out, or_5_out);
  not not_27 (not_27_out, xor_1_out);
  not not_28 (not_28_out, or_6_out);
  not not_29 (not_29_out, xor_1_out);
  not not_30 (not_30_out, or_6_out);
  not not_31 (not_31_out, or_5_out);
  not not_32 (not_32_out, xor_1_out);
  not not_33 (not_33_out, or_5_out);
  not not_34 (not_34_out, xor_1_out);
  not not_35 (not_35_out, or_6_out);
  not not_36 (not_36_out, or_5_out);
  not not_37 (not_37_out, xor_1_out);
  not not_38 (not_38_out, xor_1_out);
  not not_39 (not_39_out, or_6_out);
  not not_40 (not_40_out, xor_1_out);
  not not_41 (not_41_out, or_6_out);
  not not_42 (not_42_out, xor_1_out);
  not not_43 (not_43_out, or_5_out);
  not not_44 (not_44_out, or_6_out);
  not not_45 (not_45_out, xor_1_out);
  not not_46 (not_46_out, or_3_out);
  not not_47 (not_47_out, g_2);
  not not_48 (not_48_out, or_3_out);
  not not_49 (e_2, or_3_out);
  not not_50 (not_50_out, or_3_out);
  not not_51 (not_51_out, g_2);
  xor xor_6 (xor_6_out, in_1, in_5);
  and and_24 (and_24_out, not_26_out, not_27_out);
  and and_25 (and_25_out, or_5_out, xor_1_out);
  not not_52 (not_52_out, or_5_out);
  and and_26 (and_26_out, not_28_out, not_29_out);
  and and_27 (and_27_out, or_6_out, xor_1_out);
  or or_8 (c, not_30_out, xor_1_out, or_5_out, or_4_out);
  and and_28 (and_28_out, not_31_out, not_32_out);
  and and_29 (and_29_out, not_33_out, or_6_out);
  and and_30 (and_30_out, or_6_out, not_34_out);
  and and_31 (and_31_out, or_5_out, not_35_out, xor_1_out);
  and and_32 (and_32_out, not_36_out, not_37_out);
  and and_33 (and_33_out, or_6_out, not_38_out);
  and and_34 (and_34_out, or_4_out, or_5_out);
  and and_35 (and_35_out, not_39_out, not_40_out);
  and and_36 (and_36_out, or_5_out, not_41_out);
  and and_37 (and_37_out, or_5_out, not_42_out);
  and and_38 (and_38_out, not_43_out, or_6_out);
  and and_39 (and_39_out, or_5_out, not_44_out);
  and and_40 (and_40_out, or_5_out, not_45_out);
  or or_9 (a_2, not_46_out, g_2);
  or or_10 (c_2, not_47_out, or_3_out);
  or or_11 (d_2, not_48_out, g_2);
  and and_41 (f_2, not_50_out, not_51_out);
  xor xor_7 (xor_7_out, xor_6_out, or_7_out);
  and and_42 (and_42_out, xor_6_out, or_7_out);
  and and_43 (and_43_out, in_1, in_5);
  or or_12 (a, and_24_out, or_6_out, and_25_out, or_4_out);
  or or_13 (b, not_52_out, and_26_out, and_27_out, or_4_out);
  or or_14 (d, and_28_out, and_29_out, and_30_out, and_31_out, or_4_out);
  or or_15 (e, and_32_out, and_33_out, and_34_out);
  or or_16 (f, and_35_out, and_36_out, and_37_out, or_4_out);
  or or_17 (g, and_38_out, and_39_out, and_40_out, or_4_out);
  LED led_10 (.in(xor_7_out));
  or or_18 (or_18_out, and_42_out, and_43_out);
  LED led_11 (.in(or_18_out));

  assign b_2 = 1'b1;

  // Notes on the sheet:
  //   wynik 1 bit
  //   wynik 2bit
  //   wynik 3bit
  //   wynik 4bit
  //   wynik 5bit
endmodule
